# Fritzing sketch SliderDemo (saved by Fritzing 0.9.3b)
breadboards: 1

parts:
  Part1 = Arduino Uno (Rev3)
  R2 = Rotary Potentiometer (Small) [maximum_resistance=100kΩ package=THT]

nets:
  N1: Part1.D2, R2.wiper
  N2: Part1.5V, R2.leg2
  N3: Part1.GND, R2.leg1
